# Fritzing sketch adc_multiplexing_schematics (saved by Fritzing 1.0.4)
circuit board: 8.46667cm x 5.64444cm
stripboards: 1

parts:
  S1 = Pushbutton [package="[THT]"]
  S2 = Pushbutton [package="[THT]"]
  R5 = Resistor [tolerance=±5% power=0.25W resistance=5.1k package=THT]
  S5 = Pushbutton [package="[THT]"]
  S3 = Pushbutton [package="[THT]"]
  R1 = Resistor [tolerance=±5% power=0.25W resistance=2k package=THT]
  R2 = Resistor [tolerance=±5% power=0.25W resistance=510 package=THT]
  R4 = Resistor [tolerance=±5% power=0.25W resistance=2.2k package=THT]
  S4 = Pushbutton [package="[THT]"]
  U1 = ATTINY45 [package=dip]
  R3 = Resistor [tolerance=±5% power=0.25W resistance=680 package=THT]
  C1 = Capacitor [package=cap-pth-small2]

nets (from the schematic view):
  GND: S1.Pin_1, S1.Pin_2, S2.Pin_1, S2.Pin_2, S5.Pin_1, S5.Pin_2, S3.Pin_1, S3.Pin_2, S4.Pin_1, S4.Pin_2, U1.GND, C1.2
  N1: S1.Pin_3, S1.Pin_4, R1.Pin_0, R2.Pin_1, U1.PB2(SCK_ADC1), C1.1
  N2: S2.Pin_3, S2.Pin_4, R2.Pin_0, R3.Pin_1
  N3: R5.Pin_0, S5.Pin_3, S5.Pin_4
  N4: R5.Pin_1, R4.Pin_0, S4.Pin_3, S4.Pin_4
  N5: S3.Pin_3, S3.Pin_4, R4.Pin_1, R3.Pin_0
  N6: R1.Pin_1, U1.VCC
