# Fritzing sketch Charlieplexing 12 LEDs - Alternate version with classical schematics (saved by Fritzing 1.0.4)
breadboards: 1

parts:
  LED1 = LED - 5mm [color="Red (633nm)" current=0.030A package="5 mm [THT]"]
  LED2 = LED - 5mm [color="Red (633nm)" current=0.030A package="5 mm [THT]"]
  LED3 = LED - 5mm [color="Red (633nm)" current=0.030A package="5 mm [THT]"]
  LED6 = LED - 5mm [color="Red (633nm)" current=0.030A package="5 mm [THT]"]
  LED7 = LED - 5mm [color="Red (633nm)" current=0.030A package="5 mm [THT]"]
  LED8 = LED - 5mm [color="Red (633nm)" current=0.030A package="5 mm [THT]"]
  LED9 = LED - 5mm [color="Red (633nm)" current=0.030A package="5 mm [THT]"]
  LED10 = LED - 5mm [color="Red (633nm)" current=0.030A package="5 mm [THT]"]
  JP1 = Header 1 [package=smtso-256-et]
  JP2 = Header 1 [package=smtso-256-et]
  JP3 = Header 1 [package=smtso-256-et]
  JP4 = Header 1 [package=smtso-256-et]
  LED11 = LED - 5mm [color="Red (633nm)" current=0.030A package="5 mm [THT]"]
  LED12 = LED - 5mm [color="Red (633nm)" current=0.030A package="5 mm [THT]"]
  LED13 = LED - 5mm [color="Red (633nm)" current=0.030A package="5 mm [THT]"]
  LED14 = LED - 5mm [color="Red (633nm)" current=0.030A package="5 mm [THT]"]
  R1 = Resistor [tolerance=±5% resistance=75 package="2512 [SMD]"]
  R2 = Resistor [tolerance=±5% resistance=75 package="2512 [SMD]"]
  R3 = Resistor [tolerance=±5% resistance=75 package="2512 [SMD]"]
  R4 = Resistor [tolerance=±5% resistance=75 package="2512 [SMD]"]

nets:
  N1: LED1.cathode, LED2.anode, LED7.cathode, LED8.anode, LED13.cathode, LED14.anode, R2.Pin_1
  N2: LED1.anode, LED8.cathode, LED9.anode, LED10.cathode, LED11.cathode, LED12.anode, R1.Pin_1
  N3: LED2.cathode, LED3.anode, LED6.cathode, LED7.anode, LED11.anode, LED12.cathode, R3.Pin_1
  N4: LED3.cathode, LED6.anode, LED9.cathode, LED10.anode, LED13.anode, LED14.cathode, R4.Pin_1
  N5: JP1.1, R1.Pin_0
  N6: JP2.1, R2.Pin_0
  N7: JP3.1, R3.Pin_0
  N8: JP4.1, R4.Pin_0
