# Fritzing sketch Charlieplexing 12 LEDs - Cleaned up breadboard version (saved by Fritzing 1.0.4)
breadboards: 2

parts:
  JP1 = Header 1 [package=snap-female]
  JP2 = Header 1 [package=snap-female]
  JP3 = Header 1 [package=snap-female]
  LED2 = smd LED [color="Red (633nm)" package="0603 [SMD]"]
  LED3 = smd LED [color="Red (633nm)" package="0603 [SMD]"]
  LED4 = smd LED [color="Red (633nm)" package="0603 [SMD]"]
  LED5 = smd LED [color="Red (633nm)" package="0603 [SMD]"]
  LED6 = smd LED [color="Red (633nm)" package="0603 [SMD]"]
  LED8 = smd LED [color="Red (633nm)" package="0603 [SMD]"]
  LED7 = smd LED [color="Red (633nm)" package="0603 [SMD]"]
  LED10 = smd LED [color="Red (633nm)" package="0603 [SMD]"]
  LED9 = smd LED [color="Red (633nm)" package="0603 [SMD]"]
  R3 = Resistor [tolerance=±5% power=0.25W resistance=75 package=THT]
  R2 = Resistor [tolerance=±5% power=0.25W resistance=75 package=THT]
  JP4 = Header 1 [package=snap-female]
  R4 = Resistor [tolerance=±5% power=0.25W resistance=75 package=THT]
  LED12 = smd LED [color="Red (633nm)" package="0603 [SMD]"]
  LED11 = smd LED [color="Red (633nm)" package="0603 [SMD]"]
  LED1 = smd LED [color="Red (633nm)" package="0603 [SMD]"]
  R1 = Resistor [tolerance=±5% power=0.25W resistance=75 package=THT]

nets:
  N1: JP1.1, R1.Pin_0
  N2: JP2.1, R2.Pin_0
  N3: JP3.1, R3.Pin_0
  N4: LED2.cathode, LED3.anode, LED4.cathode, LED5.anode, LED6.cathode, LED1.anode, R1.Pin_1
  N5: LED2.anode, LED8.cathode, LED7.anode, LED10.cathode, LED9.anode, R2.Pin_1, LED1.cathode
  N6: LED3.cathode, LED4.anode, LED8.anode, LED7.cathode, R3.Pin_1, LED12.cathode, LED11.anode
  N7: LED5.cathode, LED6.anode, LED10.anode, LED9.cathode, R4.Pin_1, LED12.anode, LED11.cathode
  N8: JP4.1, R4.Pin_0
